# Fritzing sketch focuser (saved by Fritzing 1.0.2b)
circuit board: 8.46667cm x 5.64444cm
breadboards: 1

parts:
  Componente1 = Arduino Pro Mini v13
  Componente2 = EasyDriver_v44
  Grove1 = Grove OLED 128x96
  M1 = Stepper Motor - Bipolar
  J1 = female pin header, 2 pins [form="♀ (female)"]
  S1 = Pushbutton [package="[SMD]"]
  S2 = Pushbutton [package="[SMD]"]
  S3 = Pushbutton [package="[SMD]"]
  S4 = Pushbutton [package="[SMD]"]

nets:
  N1: Componente1.RAW, Componente2.VCC
  GND: Componente1.GND, Componente2.GND, Grove1.GND, J1.pin1, S1.Pin_3, S1.Pin_4, S2.Pin_3, S2.Pin_4, S3.Pin_3, S3.Pin_4, S4.Pin_3, S4.Pin_4
  VCC: Componente1.VCC, Grove1.VCC
  N2: Componente1.D9_PWM, Componente2.STEP
  N3: Componente1.D8, S1.Pin_1, S1.Pin_2
  N4: Componente1.D7, S2.Pin_1, S2.Pin_2
  N5: Componente1.D6_PWM, S3.Pin_1, S3.Pin_2
  N6: Componente1.D5_PWM, S4.Pin_1, S4.Pin_2
  N7: Componente1.D4, Componente2.DIR
  N8: Componente1.D3_PWM, Grove1.SCL
  N9: Componente1.D2, Grove1.SDA
  N10: Componente2.V+, J1.pin2
  N11: Componente2.OUT2A, M1.A
  N12: Componente2.OUT2B, M1.C
  N13: Componente2.OUT1A, M1.B
  N14: Componente2.OUT1B, M1.D
